// Logisim project CPU.circ as structural Verilog: 22 circuits, main circuit CPU
module CPU (
);

  wire add_c_out, and_1_out, and_2_out, and_3_out, and_5_out, and_7_out, and_8_out, and_9_out, and_10_out,
       and_11_out, and_12_out, and_14_out, automatic_error, bus_0, bus_1, bus_2, bus_3, bus_4, bus_5, bus_6,
       bus_7, button_1_out, button_2_out, c_add, c_in, c_out, clearMIcounter, clk, clk_direct, clock_1_out,
       clock_count_low_overflow, cmp_not_null, cmp_null, cond_always, cond_C, cond_neg, cond_not_null,
       cond_null, cond_pos, cond_selected_bit, controlled_inverter_1_out, counterOverflow,
       decrementer_1_carry, decrementer_2_carry, decrementer_3_carry, decRet, edge_detect_1_s, enableAdd,
       enableAND, enableDEC, enableInc, enableNOT, enableOR, enableSHIFTL, enableSHIFTR, enableXOR, error,
       flipLed, halt, incPC, increment_1_carry, incRet, invert_cond, loadA, loadALU, loadB, loadC, loadCmp,
       loadDisplay, loadInstruction, loadMemAddr, loadPC, loadPC_after_cond, loadRAM, loadSleep, loadU0,
       loadU1, loadU2, loadU3, manual_error, not_1_out, not_2_out, not_3_out, not_4_out, not_5_out,
       not_6_out, not_7_out, not_9_out, not_10_out, not_11_out, or_1_out, or_3_out, or_7_out, or_8_out,
       or_9_out, outA, outALU, outB, outCmp, outMemAddr, outPC, outPCp1, outRAM, outRetAddr, outU0, outU1,
       outU2, outU3, pause, por_1_out, reset, ripplecarryadder_1_c_out, selected_bit, selector0, selector1,
       selector2, shiftleft_1_carry, shiftright_1_carry, storeRAM, t_ff_1_q;
  wire [3:0] add_s, add_s_2, clock_count_high_value, clock_count_high_value_2, clock_count_low_value,
       clock_count_low_value_2, ret_addr_reg_value, ret_addr_reg_value_2, ripplecarryadder_1_s,
       ripplecarryadder_1_s_2, sleep_decounter_o, sleep_decounter_o_2;
  wire [7:0] A, alu_reg_o, and_4_out, B, byteand_1_o, bytenot_1_o, byteor_1_y, bytexor_1_y, CMP,
       controlled_buffer_1_out, controlled_buffer_3_out, controlled_buffer_17_out, controlled_buffer_33_out,
       controlled_buffer_35_out, counter8_1_value_p1, decrementer_1_o, decrementer_2_o, display_o,
       increment_1_o, instruction_reg_o, mem_addr_bus, memory_dout, mi_counter_value, PC, pla_1_out,
       pla_2_out, pla_3_out, pla_4_out, selector_decoder_out, shiftleft_1_o, shiftright_1_o, U0_o, U1_o,
       U2_o, U3_o;
  wire [30:23] rom_1_data;

  not not_1 (not_1_out, reset);
  assign controlled_buffer_1_out = storeRAM ? mem_addr_bus : 8'bz;  // Controlled_Buffer controlled_buffer_1
  assign controlled_buffer_1_out = loadRAM ? {bus_7, bus_6, bus_5, bus_4, bus_3, bus_2, bus_1, bus_0} : 8'bz;  // Controlled_Buffer controlled_buffer_2
  assign controlled_buffer_3_out = storeRAM ? {bus_7, bus_6, bus_5, bus_4, bus_3, bus_2, bus_1, bus_0} : 8'bz;  // Controlled_Buffer controlled_buffer_3
  and and_1 (and_1_out, clk, not_1_out);
  not not_2 (not_2_out, and_1_out);
  Hex_Digit_Display hex_digit_display_1 (.value(controlled_buffer_1_out[7:4]));  // open: dp
  not not_3 (not_3_out, storeRAM);
  or or_1 (or_1_out, reset, clearMIcounter, 1'b0);
  Hex_Digit_Display hex_digit_display_2 (.value(controlled_buffer_1_out[3:0]));  // open: dp
  RAM #(.databus("bibus")) memory (
    .addr(controlled_buffer_1_out), .we(storeRAM), .oe(not_3_out), .clk(clk), .din(controlled_buffer_3_out),
    .dout(memory_dout));
  ByteRegisterSafer mem_addr_reg (
    .o(mem_addr_bus), .load(loadMemAddr), .clock(clk),
    .i({bus_7, bus_6, bus_5, bus_4, bus_3, bus_2, bus_1, bus_0}), .clear(reset));
  Hex_Digit_Display hex_digit_display_3 (.value(mem_addr_bus[7:4]));  // open: dp
  Hex_Digit_Display hex_digit_display_4 (.value(mem_addr_bus[3:0]));  // open: dp
  Counter8 mi_counter (
    .value(mi_counter_value), .inc(not_2_out), .clock(not_2_out), .clear(or_1_out));  // open: overflow, value_p1, dec, load, i
  ByteRegisterSafer instruction_reg (
    .o(instruction_reg_o), .load(loadInstruction), .clock(clk),
    .i({bus_7, bus_6, bus_5, bus_4, bus_3, bus_2, bus_1, bus_0}), .clear(reset));
  Hex_Digit_Display hex_digit_display_5 (.value(memory_dout[7:4]));  // open: dp
  Hex_Digit_Display hex_digit_display_6 (.value(memory_dout[3:0]));  // open: dp
  Clock clock_1 (.out(clock_1_out));
  Button button_1 (.out(button_1_out));
  assign {bus_7, bus_6, bus_5, bus_4, bus_3, bus_2, bus_1, bus_0} = outRAM ? memory_dout : 8'bz;  // Controlled_Buffer controlled_buffer_4
  assign {bus_7, bus_6, bus_5, bus_4, bus_3, bus_2, bus_1, bus_0} = outMemAddr ? mem_addr_bus : 8'bz;  // Controlled_Buffer controlled_buffer_5
  PLA #(.in_width(1), .out_width(8), .\table ("0 10000000\n1 00111110")) pla_1 (.in(error), .out(pla_1_out));
  Hex_Digit_Display hex_digit_display_7 (.value(instruction_reg_o[7:4]));  // open: dp
  Hex_Digit_Display hex_digit_display_8 (.value(instruction_reg_o[3:0]));  // open: dp
  POR #(.PorHighDuration(1)) por_1 (.out(por_1_out));
  or or_2 (clk_direct, clock_1_out, button_1_out);
  or or_3 (or_3_out, halt, automatic_error, pause);
  not not_4 (not_4_out, or_3_out);
  _7_Segment_Display u_7_segment_display_1 (
    .g(pla_1_out[3]), .f(pla_1_out[2]), .a(pla_1_out[1]), .b(pla_1_out[0]), .e(pla_1_out[4]),
    .d(pla_1_out[5]), .c(pla_1_out[6]), .dp(pla_1_out[7]));
  Button button_2 (.out(button_2_out));
  ROM #(.addrWidth(12), .dataWidth(32)) instruction_decoder (
    .addr({instruction_reg_o, mi_counter_value[3:0]}),
    .data({storeRAM, cond_pos, cond_not_null, enableInc, invert_cond, cond_null, cond_neg, cond_always, enableXOR, outPCp1, outCmp, loadCmp, loadALU, enableNOT, outB, outA, loadPC, outRetAddr, incRet, outMemAddr, loadMemAddr, loadInstruction, outALU, enableAdd, clearMIcounter, loadB, loadA, outRAM, outPC, loadRAM, incPC, halt}));
  ROM #(.addrWidth(12), .dataWidth(32)) rom_1 (
    .addr({instruction_reg_o, mi_counter_value[3:0]}),
    .data({manual_error, rom_1_data, decRet, loadSleep, enableDEC, cond_C, loadC, loadDisplay, flipLed, outU3, loadU3, outU2, loadU2, outU1, loadU1, cond_selected_bit, selector2, selector1, selector0, loadU0, outU0, enableAND, enableSHIFTR, enableSHIFTL, enableOR}));
  edge_detect edge_detect_1 (.s(edge_detect_1_s), .i(por_1_out));
  and and_2 (and_2_out, clk_direct, not_4_out);
  Hex_Digit_Display hex_digit_display_9 (.value({bus_7, bus_6, bus_5, bus_4}));  // open: dp
  Hex_Digit_Display hex_digit_display_10 (.value({bus_3, bus_2, bus_1, bus_0}));  // open: dp
  T_Flip_Flop t_ff_1 (.T(flipLed), .clk(clk), .Q(t_ff_1_q), .reset(reset));  // open: Qn, preset
  or or_4 (reset, edge_detect_1_s, button_2_out);
  or or_5 (clk, reset, and_2_out);
  LED led_1 (.in(t_ff_1_q));
  or or_6 (error, manual_error, automatic_error);
  assign {bus_7, bus_6, bus_5, bus_4, bus_3, bus_2, bus_1, bus_0} = reset ? {8{1'b0}} : 8'bz;  // Controlled_Buffer controlled_buffer_6
  LED led_2 (.in(clk));
  Hex_Digit_Display hex_digit_display_11 (.value(A[7:4]));  // open: dp
  Hex_Digit_Display hex_digit_display_12 (.value(A[3:0]));  // open: dp
  ByteRegisterSafer byteregistersafer_1 (
    .o(A), .load(loadA), .clock(clk), .i({bus_7, bus_6, bus_5, bus_4, bus_3, bus_2, bus_1, bus_0}),
    .clear(reset));
  ByteRegisterSafer byteregistersafer_2 (
    .o(B), .load(loadB), .clock(clk), .i({bus_7, bus_6, bus_5, bus_4, bus_3, bus_2, bus_1, bus_0}),
    .clear(reset));
  ByteRegisterSafer U0 (
    .o(U0_o), .load(loadU0), .clock(clk), .i({bus_7, bus_6, bus_5, bus_4, bus_3, bus_2, bus_1, bus_0}),
    .clear(reset));
  ByteRegisterSafer U1 (
    .o(U1_o), .load(loadU1), .clock(clk), .i({bus_7, bus_6, bus_5, bus_4, bus_3, bus_2, bus_1, bus_0}),
    .clear(reset));
  ByteRegisterSafer U2 (
    .o(U2_o), .load(loadU2), .clock(clk), .i({bus_7, bus_6, bus_5, bus_4, bus_3, bus_2, bus_1, bus_0}),
    .clear(reset));
  assign {bus_7, bus_6, bus_5, bus_4, bus_3, bus_2, bus_1, bus_0} = outA ? A : 8'bz;  // Controlled_Buffer controlled_buffer_7
  Hex_Digit_Display hex_digit_display_13 (.value(B[7:4]));  // open: dp
  Hex_Digit_Display hex_digit_display_14 (.value(B[3:0]));  // open: dp
  Hex_Digit_Display hex_digit_display_15 (.value(U0_o[7:4]));  // open: dp
  Hex_Digit_Display hex_digit_display_16 (.value(U0_o[3:0]));  // open: dp
  Hex_Digit_Display hex_digit_display_17 (.value(U1_o[7:4]));  // open: dp
  Hex_Digit_Display hex_digit_display_18 (.value(U1_o[3:0]));  // open: dp
  Hex_Digit_Display hex_digit_display_19 (.value(U2_o[7:4]));  // open: dp
  Hex_Digit_Display hex_digit_display_20 (.value(U2_o[3:0]));  // open: dp
  Hex_Digit_Display hex_digit_display_21 (.value(PC[7:4]));  // open: dp
  Hex_Digit_Display hex_digit_display_22 (.value(PC[3:0]));  // open: dp
  Counter8 counter8_1 (
    .overflow(counterOverflow), .value_p1(counter8_1_value_p1), .value(PC), .load(loadPC_after_cond),
    .inc(incPC), .clock(clk), .i({bus_7, bus_6, bus_5, bus_4, bus_3, bus_2, bus_1, bus_0}), .clear(reset));  // open: dec
  assign {bus_7, bus_6, bus_5, bus_4, bus_3, bus_2, bus_1, bus_0} = outB ? B : 8'bz;  // Controlled_Buffer controlled_buffer_8
  assign {bus_7, bus_6, bus_5, bus_4, bus_3, bus_2, bus_1, bus_0} = outU0 ? U0_o : 8'bz;  // Controlled_Buffer controlled_buffer_9
  assign {bus_7, bus_6, bus_5, bus_4, bus_3, bus_2, bus_1, bus_0} = outU1 ? U1_o : 8'bz;  // Controlled_Buffer controlled_buffer_10
  assign {bus_7, bus_6, bus_5, bus_4, bus_3, bus_2, bus_1, bus_0} = outU2 ? U2_o : 8'bz;  // Controlled_Buffer controlled_buffer_11
  assign {bus_7, bus_6, bus_5, bus_4, bus_3, bus_2, bus_1, bus_0} = outPCp1 ? counter8_1_value_p1 : 8'bz;  // Controlled_Buffer controlled_buffer_12
  assign {bus_7, bus_6, bus_5, bus_4, bus_3, bus_2, bus_1, bus_0} = outPC ? PC : 8'bz;  // Controlled_Buffer controlled_buffer_13
  or or_7 (or_7_out, loadC, enableAdd);
  PLA #(.in_width(3), .out_width(8), .\table ("000 00000001\n001 00000010\n010 00000100\n011 00001000\n100 00010000\n101 00100000\n110 01000000\n111 10000000")) selector_decoder (
    .in({selector2, selector1, selector0}), .out(selector_decoder_out));
  ByteRegisterSafer U3 (
    .o(U3_o), .load(loadU3), .clock(clk), .i({bus_7, bus_6, bus_5, bus_4, bus_3, bus_2, bus_1, bus_0}),
    .clear(reset));
  and and_3 (and_3_out, or_7_out, clk);
  assign and_4_out = selector_decoder_out & CMP;  // AND_Gate and_4, 8 bits wide
  Hex_Digit_Display hex_digit_display_23 (.value(U3_o[7:4]));  // open: dp
  Hex_Digit_Display hex_digit_display_24 (.value(U3_o[3:0]));  // open: dp
  D_Flip_Flop C (.D(c_in), .clk(and_3_out), .Q(c_out));  // open: Qn, preset, reset
  NotNull notnull_1 (.i(and_4_out), .not_null(selected_bit));  // open: is_null
  assign {bus_7, bus_6, bus_5, bus_4, bus_3, bus_2, bus_1, bus_0} = outU3 ? U3_o : 8'bz;  // Controlled_Buffer controlled_buffer_14
  Hex_Digit_Display hex_digit_display_25 (.value(ret_addr_reg_value_2));  // open: dp
  Hex_Digit_Display hex_digit_display_26 (.value(ret_addr_reg_value));  // open: dp
  Counter8 ret_addr_reg (
    .value({ret_addr_reg_value_2, ret_addr_reg_value}), .dec(decRet), .inc(incRet), .clock(clk), .clear(reset));  // open: overflow, value_p1, load, i
  not not_5 (not_5_out, CMP[7]);
  Hex_Digit_Display hex_digit_display_27 (.value(ripplecarryadder_1_s_2));  // open: dp
  RippleCarryAdder ripplecarryadder_1 (
    .c_out(ripplecarryadder_1_c_out), .s({ripplecarryadder_1_s_2, ripplecarryadder_1_s}),
    .b({ret_addr_reg_value_2, ret_addr_reg_value}), .a(8'hf8));
  and and_5 (and_5_out, not_5_out, cond_pos);
  Hex_Digit_Display hex_digit_display_28 (.value(ripplecarryadder_1_s));  // open: dp
  assign {bus_7, bus_6, bus_5, bus_4, bus_3, bus_2, bus_1, bus_0} = outRetAddr ? {ripplecarryadder_1_s_2, ripplecarryadder_1_s} : 8'bz;  // Controlled_Buffer controlled_buffer_15
  and and_6 (automatic_error, ripplecarryadder_1_c_out, outRetAddr);
  Hex_Digit_Display hex_digit_display_29 (.value(add_s_2));  // open: dp
  Hex_Digit_Display hex_digit_display_30 (.value(add_s));  // open: dp
  RippleCarryAdder add (
    .c_out(add_c_out), .s({add_s_2, add_s}), .b({bus_7, bus_6, bus_5, bus_4, bus_3, bus_2, bus_1, bus_0}),
    .a(B));
  assign c_add = enableAdd ? add_c_out : 1'bz;  // Controlled_Buffer controlled_buffer_16
  Increment increment_1 (
    .carry(increment_1_carry), .o(increment_1_o), .i({bus_7, bus_6, bus_5, bus_4, bus_3, bus_2, bus_1, bus_0}));
  ShiftRight shiftright_1 (
    .i({bus_7, bus_6, bus_5, bus_4, bus_3, bus_2, bus_1, bus_0}), .carry(shiftright_1_carry),
    .o(shiftright_1_o));
  and and_7 (and_7_out, cond_null, cmp_null);
  and and_8 (and_8_out, cond_selected_bit, selected_bit);
  and and_9 (and_9_out, cond_neg, CMP[7]);
  not not_6 (not_6_out, cond_not_null);
  and and_10 (and_10_out, cond_not_null, cmp_not_null);
  assign controlled_buffer_17_out = enableAdd ? {add_s_2, add_s} : 8'bz;  // Controlled_Buffer controlled_buffer_17
  assign c_in = enableInc ? increment_1_carry : 1'bz;  // Controlled_Buffer controlled_buffer_18
  ByteOr byteor_1 (.a({bus_7, bus_6, bus_5, bus_4, bus_3, bus_2, bus_1, bus_0}), .b(B), .y(byteor_1_y));
  ShiftLeft shiftleft_1 (
    .i({bus_7, bus_6, bus_5, bus_4, bus_3, bus_2, bus_1, bus_0}), .carry(shiftleft_1_carry), .o(shiftleft_1_o));
  assign controlled_buffer_17_out = enableSHIFTL ? shiftleft_1_o : 8'bz;  // Controlled_Buffer controlled_buffer_19
  assign c_in = enableSHIFTR ? shiftright_1_carry : 1'bz;  // Controlled_Buffer controlled_buffer_20
  assign controlled_buffer_17_out = enableSHIFTR ? shiftright_1_o : 8'bz;  // Controlled_Buffer controlled_buffer_21
  assign c_in = enableDEC ? decrementer_1_carry : 1'bz;  // Controlled_Buffer controlled_buffer_22
  Decrementer decrementer_1 (
    .i({bus_7, bus_6, bus_5, bus_4, bus_3, bus_2, bus_1, bus_0}), .carry(decrementer_1_carry),
    .o(decrementer_1_o));
  or or_8 (or_8_out, not_6_out, and_10_out);
  assign controlled_buffer_17_out = enableNOT ? bytenot_1_o : 8'bz;  // Controlled_Buffer controlled_buffer_23
  ByteNot bytenot_1 (.i({bus_7, bus_6, bus_5, bus_4, bus_3, bus_2, bus_1, bus_0}), .o(bytenot_1_o));
  assign controlled_buffer_17_out = enableXOR ? bytexor_1_y : 8'bz;  // Controlled_Buffer controlled_buffer_24
  ByteXor bytexor_1 (.a({bus_7, bus_6, bus_5, bus_4, bus_3, bus_2, bus_1, bus_0}), .b(B), .y(bytexor_1_y));
  assign controlled_buffer_17_out = enableInc ? increment_1_o : 8'bz;  // Controlled_Buffer controlled_buffer_25
  assign controlled_buffer_17_out = enableOR ? byteor_1_y : 8'bz;  // Controlled_Buffer controlled_buffer_26
  assign c_in = enableSHIFTL ? shiftleft_1_carry : 1'bz;  // Controlled_Buffer controlled_buffer_27
  assign controlled_buffer_17_out = enableAND ? byteand_1_o : 8'bz;  // Controlled_Buffer controlled_buffer_28
  ByteAnd byteand_1 (.a({bus_7, bus_6, bus_5, bus_4, bus_3, bus_2, bus_1, bus_0}), .b(B), .o(byteand_1_o));
  assign controlled_buffer_17_out = enableDEC ? decrementer_1_o : 8'bz;  // Controlled_Buffer controlled_buffer_29
  and and_11 (and_11_out, and_9_out, or_8_out);
  and and_12 (and_12_out, cond_C, c_out);
  or or_9 (or_9_out, cond_always, and_7_out, and_8_out, and_5_out, and_11_out, and_12_out);
  Hex_Digit_Display hex_digit_display_31 (.value(controlled_buffer_17_out[7:4]));  // open: dp
  Hex_Digit_Display hex_digit_display_32 (.value(controlled_buffer_17_out[3:0]));  // open: dp
  assign controlled_inverter_1_out = invert_cond ? ~or_9_out : 1'bz;  // Controlled_Inverter controlled_inverter_1
  assign controlled_inverter_1_out = not_7_out ? or_9_out : 1'bz;  // Controlled_Buffer controlled_buffer_30
  not not_7 (not_7_out, invert_cond);
  ByteRegisterSafer cmp_reg (
    .o(CMP), .load(loadCmp), .clock(clk), .i({bus_7, bus_6, bus_5, bus_4, bus_3, bus_2, bus_1, bus_0}),
    .clear(reset));
  Hex_Digit_Display hex_digit_display_33 (.value(alu_reg_o[7:4]));  // open: dp
  Hex_Digit_Display hex_digit_display_34 (.value(alu_reg_o[3:0]));  // open: dp
  ByteRegisterSafer alu_reg (.o(alu_reg_o), .load(loadALU), .clock(clk), .i(controlled_buffer_17_out), .clear(reset));
  Hex_Digit_Display hex_digit_display_35 (.value(CMP[7:4]));  // open: dp
  Hex_Digit_Display hex_digit_display_36 (.value(CMP[3:0]));  // open: dp
  and and_13 (loadPC_after_cond, loadPC, controlled_inverter_1_out);
  assign {bus_7, bus_6, bus_5, bus_4, bus_3, bus_2, bus_1, bus_0} = outALU ? alu_reg_o : 8'bz;  // Controlled_Buffer controlled_buffer_31
  or or_10 (cmp_not_null, CMP[7], CMP[6], CMP[5], CMP[4], CMP[3], CMP[2], CMP[1], CMP[0]);
  not not_8 (cmp_null, cmp_not_null);
  assign {bus_7, bus_6, bus_5, bus_4, bus_3, bus_2, bus_1, bus_0} = outCmp ? CMP : 8'bz;  // Controlled_Buffer controlled_buffer_32
  not not_9 (not_9_out, clk);
  assign controlled_buffer_33_out = loadSleep ? {bus_7, bus_6, bus_5, bus_4, bus_3, bus_2, bus_1, bus_0} : 8'bz;  // Controlled_Buffer controlled_buffer_33
  not not_10 (not_10_out, loadSleep);
  PLA #(.in_width(8), .out_width(8), .\table ("00000000 01110111 # 0\n00000001 01000001 # 1\n00000010 00111011 # 2\n00000011 01101011 # 3\n00000100 01001101 # 4\n00000101 01101110 # 5\n00000110 01111110 # 6\n00000111 01000011 # 7\n00001000 01111111 # 8\n00001001 01101111 # 9\n00001010 01110111 # 10\n00001011 01000001 # 11\n00001100 00111011 # 12\n00001101 01101011 # 13\n00001110 01001101 # 14\n00001111 01101110 # 15\n00010000 01111110 # 16\n00010001 01000011 # 17\n00010010 01111111 # 18\n00010011 01101111 # 19\n00010100 01110111 # 20\n00010101 01000001 # 21\n00010110 00111011 # 22\n00010111 01101011 # 23\n00011000 01001101 # 24\n00011001 01101110 # 25\n00011010 01111110 # 26\n00011011 01000011 # 27\n00011100 01111111 # 28\n00011101 01101111 # 29\n00011110 01110111 # 30\n00011111 01000001 # 31\n00100000 00111011 # 32\n00100001 01101011 # 33\n00100010 01001101 # 34\n00100011 01101110 # 35\n00100100 01111110 # 36\n00100101 01000011 # 37\n00100110 01111111 # 38\n00100111 01101111 # 39\n00101000 01110111 # 40\n00101001 01000001 # 41\n00101010 00111011 # 42\n00101011 01101011 # 43\n00101100 01001101 # 44\n00101101 01101110 # 45\n00101110 01111110 # 46\n00101111 01000011 # 47\n00110000 01111111 # 48\n00110001 01101111 # 49\n00110010 01110111 # 50\n00110011 01000001 # 51\n00110100 00111011 # 52\n00110101 01101011 # 53\n00110110 01001101 # 54\n00110111 01101110 # 55\n00111000 01111110 # 56\n00111001 01000011 # 57\n00111010 01111111 # 58\n00111011 01101111 # 59\n00111100 01110111 # 60\n00111101 01000001 # 61\n00111110 00111011 # 62\n00111111 01101011 # 63\n01000000 01001101 # 64\n01000001 01101110 # 65\n01000010 01111110 # 66\n01000011 01000011 # 67\n01000100 01111111 # 68\n01000101 01101111 # 69\n01000110 01110111 # 70\n01000111 01000001 # 71\n01001000 00111011 # 72\n01001001 01101011 # 73\n01001010 01001101 # 74\n01001011 01101110 # 75\n01001100 01111110 # 76\n01001101 01000011 # 77\n01001110 01111111 # 78\n01001111 01101111 # 79\n01010000 01110111 # 80\n01010001 01000001 # 81\n01010010 00111011 # 82\n01010011 01101011 # 83\n01010100 01001101 # 84\n01010101 01101110 # 85\n01010110 01111110 # 86\n01010111 01000011 # 87\n01011000 01111111 # 88\n01011001 01101111 # 89\n01011010 01110111 # 90\n01011011 01000001 # 91\n01011100 00111011 # 92\n01011101 01101011 # 93\n01011110 01001101 # 94\n01011111 01101110 # 95\n01100000 01111110 # 96\n01100001 01000011 # 97\n01100010 01111111 # 98\n01100011 01101111 # 99\n01100100 01110111 # 100\n01100101 01000001 # 101\n01100110 00111011 # 102\n01100111 01101011 # 103\n01101000 01001101 # 104\n01101001 01101110 # 105\n01101010 01111110 # 106\n01101011 01000011 # 107\n01101100 01111111 # 108\n01101101 01101111 # 109\n01101110 01110111 # 110\n01101111 01000001 # 111\n01110000 00111011 # 112\n01110001 01101011 # 113\n01110010 01001101 # 114\n01110011 01101110 # 115\n01110100 01111110 # 116\n01110101 01000011 # 117\n01110110 01111111 # 118\n01110111 01101111 # 119\n01111000 01110111 # 120\n01111001 01000001 # 121\n01111010 00111011 # 122\n01111011 01101011 # 123\n01111100 01001101 # 124\n01111101 01101110 # 125\n01111110 01111110 # 126\n01111111 01000011 # 127\n10000000 01111111 # 128\n10000001 01101111 # 129\n10000010 01110111 # 130\n10000011 01000001 # 131\n10000100 00111011 # 132\n10000101 01101011 # 133\n10000110 01001101 # 134\n10000111 01101110 # 135\n10001000 01111110 # 136\n10001001 01000011 # 137\n10001010 01111111 # 138\n10001011 01101111 # 139\n10001100 01110111 # 140\n10001101 01000001 # 141\n10001110 00111011 # 142\n10001111 01101011 # 143\n10010000 01001101 # 144\n10010001 01101110 # 145\n10010010 01111110 # 146\n10010011 01000011 # 147\n10010100 01111111 # 148\n10010101 01101111 # 149\n10010110 01110111 # 150\n10010111 01000001 # 151\n10011000 00111011 # 152\n10011001 01101011 # 153\n10011010 01001101 # 154\n10011011 01101110 # 155\n10011100 01111110 # 156\n10011101 01000011 # 157\n10011110 01111111 # 158\n10011111 01101111 # 159\n10100000 01110111 # 160\n10100001 01000001 # 161\n10100010 00111011 # 162\n10100011 01101011 # 163\n10100100 01001101 # 164\n10100101 01101110 # 165\n10100110 01111110 # 166\n10100111 01000011 # 167\n10101000 01111111 # 168\n10101001 01101111 # 169\n10101010 01110111 # 170\n10101011 01000001 # 171\n10101100 00111011 # 172\n10101101 01101011 # 173\n10101110 01001101 # 174\n10101111 01101110 # 175\n10110000 01111110 # 176\n10110001 01000011 # 177\n10110010 01111111 # 178\n10110011 01101111 # 179\n10110100 01110111 # 180\n10110101 01000001 # 181\n10110110 00111011 # 182\n10110111 01101011 # 183\n10111000 01001101 # 184\n10111001 01101110 # 185\n10111010 01111110 # 186\n10111011 01000011 # 187\n10111100 01111111 # 188\n10111101 01101111 # 189\n10111110 01110111 # 190\n10111111 01000001 # 191\n11000000 00111011 # 192\n11000001 01101011 # 193\n11000010 01001101 # 194\n11000011 01101110 # 195\n11000100 01111110 # 196\n11000101 01000011 # 197\n11000110 01111111 # 198\n11000111 01101111 # 199\n11001000 01110111 # 200\n11001001 01000001 # 201\n11001010 00111011 # 202\n11001011 01101011 # 203\n11001100 01001101 # 204\n11001101 01101110 # 205\n11001110 01111110 # 206\n11001111 01000011 # 207\n11010000 01111111 # 208\n11010001 01101111 # 209\n11010010 01110111 # 210\n11010011 01000001 # 211\n11010100 00111011 # 212\n11010101 01101011 # 213\n11010110 01001101 # 214\n11010111 01101110 # 215\n11011000 01111110 # 216\n11011001 01000011 # 217\n11011010 01111111 # 218\n11011011 01101111 # 219\n11011100 01110111 # 220\n11011101 01000001 # 221\n11011110 00111011 # 222\n11011111 01101011 # 223\n11100000 01001101 # 224\n11100001 01101110 # 225\n11100010 01111110 # 226\n11100011 01000011 # 227\n11100100 01111111 # 228\n11100101 01101111 # 229\n11100110 01110111 # 230\n11100111 01000001 # 231\n11101000 00111011 # 232\n11101001 01101011 # 233\n11101010 01001101 # 234\n11101011 01101110 # 235\n11101100 01111110 # 236\n11101101 01000011 # 237\n11101110 01111111 # 238\n11101111 01101111 # 239\n11110000 01110111 # 240\n11110001 01000001 # 241\n11110010 00111011 # 242\n11110011 01101011 # 243\n11110100 01001101 # 244\n11110101 01101110 # 245\n11110110 01111110 # 246\n11110111 01000011 # 247\n11111000 01111111 # 248\n11111001 01101111 # 249\n11111010 01110111 # 250\n11111011 01000001 # 251\n11111100 00111011 # 252\n11111101 01101011 # 253\n11111110 01001101 # 254\n11111111 01101110 # 255")) pla_2 (
    .in(display_o), .out(pla_2_out));
  PLA #(.in_width(8), .out_width(8), .\table ("00000000 01110111 # 0\n00000001 01110111 # 1\n00000010 01110111 # 2\n00000011 01110111 # 3\n00000100 01110111 # 4\n00000101 01110111 # 5\n00000110 01110111 # 6\n00000111 01110111 # 7\n00001000 01110111 # 8\n00001001 01110111 # 9\n00001010 01000001 # 10\n00001011 01000001 # 11\n00001100 01000001 # 12\n00001101 01000001 # 13\n00001110 01000001 # 14\n00001111 01000001 # 15\n00010000 01000001 # 16\n00010001 01000001 # 17\n00010010 01000001 # 18\n00010011 01000001 # 19\n00010100 00111011 # 20\n00010101 00111011 # 21\n00010110 00111011 # 22\n00010111 00111011 # 23\n00011000 00111011 # 24\n00011001 00111011 # 25\n00011010 00111011 # 26\n00011011 00111011 # 27\n00011100 00111011 # 28\n00011101 00111011 # 29\n00011110 01101011 # 30\n00011111 01101011 # 31\n00100000 01101011 # 32\n00100001 01101011 # 33\n00100010 01101011 # 34\n00100011 01101011 # 35\n00100100 01101011 # 36\n00100101 01101011 # 37\n00100110 01101011 # 38\n00100111 01101011 # 39\n00101000 01001101 # 40\n00101001 01001101 # 41\n00101010 01001101 # 42\n00101011 01001101 # 43\n00101100 01001101 # 44\n00101101 01001101 # 45\n00101110 01001101 # 46\n00101111 01001101 # 47\n00110000 01001101 # 48\n00110001 01001101 # 49\n00110010 01101110 # 50\n00110011 01101110 # 51\n00110100 01101110 # 52\n00110101 01101110 # 53\n00110110 01101110 # 54\n00110111 01101110 # 55\n00111000 01101110 # 56\n00111001 01101110 # 57\n00111010 01101110 # 58\n00111011 01101110 # 59\n00111100 01111110 # 60\n00111101 01111110 # 61\n00111110 01111110 # 62\n00111111 01111110 # 63\n01000000 01111110 # 64\n01000001 01111110 # 65\n01000010 01111110 # 66\n01000011 01111110 # 67\n01000100 01111110 # 68\n01000101 01111110 # 69\n01000110 01000011 # 70\n01000111 01000011 # 71\n01001000 01000011 # 72\n01001001 01000011 # 73\n01001010 01000011 # 74\n01001011 01000011 # 75\n01001100 01000011 # 76\n01001101 01000011 # 77\n01001110 01000011 # 78\n01001111 01000011 # 79\n01010000 01111111 # 80\n01010001 01111111 # 81\n01010010 01111111 # 82\n01010011 01111111 # 83\n01010100 01111111 # 84\n01010101 01111111 # 85\n01010110 01111111 # 86\n01010111 01111111 # 87\n01011000 01111111 # 88\n01011001 01111111 # 89\n01011010 01101111 # 90\n01011011 01101111 # 91\n01011100 01101111 # 92\n01011101 01101111 # 93\n01011110 01101111 # 94\n01011111 01101111 # 95\n01100000 01101111 # 96\n01100001 01101111 # 97\n01100010 01101111 # 98\n01100011 01101111 # 99\n01100100 01110111 # 100\n01100101 01110111 # 101\n01100110 01110111 # 102\n01100111 01110111 # 103\n01101000 01110111 # 104\n01101001 01110111 # 105\n01101010 01110111 # 106\n01101011 01110111 # 107\n01101100 01110111 # 108\n01101101 01110111 # 109\n01101110 01000001 # 110\n01101111 01000001 # 111\n01110000 01000001 # 112\n01110001 01000001 # 113\n01110010 01000001 # 114\n01110011 01000001 # 115\n01110100 01000001 # 116\n01110101 01000001 # 117\n01110110 01000001 # 118\n01110111 01000001 # 119\n01111000 00111011 # 120\n01111001 00111011 # 121\n01111010 00111011 # 122\n01111011 00111011 # 123\n01111100 00111011 # 124\n01111101 00111011 # 125\n01111110 00111011 # 126\n01111111 00111011 # 127\n10000000 00111011 # 128\n10000001 00111011 # 129\n10000010 01101011 # 130\n10000011 01101011 # 131\n10000100 01101011 # 132\n10000101 01101011 # 133\n10000110 01101011 # 134\n10000111 01101011 # 135\n10001000 01101011 # 136\n10001001 01101011 # 137\n10001010 01101011 # 138\n10001011 01101011 # 139\n10001100 01001101 # 140\n10001101 01001101 # 141\n10001110 01001101 # 142\n10001111 01001101 # 143\n10010000 01001101 # 144\n10010001 01001101 # 145\n10010010 01001101 # 146\n10010011 01001101 # 147\n10010100 01001101 # 148\n10010101 01001101 # 149\n10010110 01101110 # 150\n10010111 01101110 # 151\n10011000 01101110 # 152\n10011001 01101110 # 153\n10011010 01101110 # 154\n10011011 01101110 # 155\n10011100 01101110 # 156\n10011101 01101110 # 157\n10011110 01101110 # 158\n10011111 01101110 # 159\n10100000 01111110 # 160\n10100001 01111110 # 161\n10100010 01111110 # 162\n10100011 01111110 # 163\n10100100 01111110 # 164\n10100101 01111110 # 165\n10100110 01111110 # 166\n10100111 01111110 # 167\n10101000 01111110 # 168\n10101001 01111110 # 169\n10101010 01000011 # 170\n10101011 01000011 # 171\n10101100 01000011 # 172\n10101101 01000011 # 173\n10101110 01000011 # 174\n10101111 01000011 # 175\n10110000 01000011 # 176\n10110001 01000011 # 177\n10110010 01000011 # 178\n10110011 01000011 # 179\n10110100 01111111 # 180\n10110101 01111111 # 181\n10110110 01111111 # 182\n10110111 01111111 # 183\n10111000 01111111 # 184\n10111001 01111111 # 185\n10111010 01111111 # 186\n10111011 01111111 # 187\n10111100 01111111 # 188\n10111101 01111111 # 189\n10111110 01101111 # 190\n10111111 01101111 # 191\n11000000 01101111 # 192\n11000001 01101111 # 193\n11000010 01101111 # 194\n11000011 01101111 # 195\n11000100 01101111 # 196\n11000101 01101111 # 197\n11000110 01101111 # 198\n11000111 01101111 # 199\n11001000 01110111 # 200\n11001001 01110111 # 201\n11001010 01110111 # 202\n11001011 01110111 # 203\n11001100 01110111 # 204\n11001101 01110111 # 205\n11001110 01110111 # 206\n11001111 01110111 # 207\n11010000 01110111 # 208\n11010001 01110111 # 209\n11010010 01000001 # 210\n11010011 01000001 # 211\n11010100 01000001 # 212\n11010101 01000001 # 213\n11010110 01000001 # 214\n11010111 01000001 # 215\n11011000 01000001 # 216\n11011001 01000001 # 217\n11011010 01000001 # 218\n11011011 01000001 # 219\n11011100 00111011 # 220\n11011101 00111011 # 221\n11011110 00111011 # 222\n11011111 00111011 # 223\n11100000 00111011 # 224\n11100001 00111011 # 225\n11100010 00111011 # 226\n11100011 00111011 # 227\n11100100 00111011 # 228\n11100101 00111011 # 229\n11100110 01101011 # 230\n11100111 01101011 # 231\n11101000 01101011 # 232\n11101001 01101011 # 233\n11101010 01101011 # 234\n11101011 01101011 # 235\n11101100 01101011 # 236\n11101101 01101011 # 237\n11101110 01101011 # 238\n11101111 01101011 # 239\n11110000 01001101 # 240\n11110001 01001101 # 241\n11110010 01001101 # 242\n11110011 01001101 # 243\n11110100 01001101 # 244\n11110101 01001101 # 245\n11110110 01001101 # 246\n11110111 01001101 # 247\n11111000 01001101 # 248\n11111001 01001101 # 249\n11111010 01101110 # 250\n11111011 01101110 # 251\n11111100 01101110 # 252\n11111101 01101110 # 253\n11111110 01101110 # 254\n11111111 01101110 # 255")) pla_3 (
    .in(display_o), .out(pla_3_out));
  PLA #(.in_width(8), .out_width(8), .\table ("00000000 01110111 # 0\n00000001 01110111 # 1\n00000010 01110111 # 2\n00000011 01110111 # 3\n00000100 01110111 # 4\n00000101 01110111 # 5\n00000110 01110111 # 6\n00000111 01110111 # 7\n00001000 01110111 # 8\n00001001 01110111 # 9\n00001010 01110111 # 10\n00001011 01110111 # 11\n00001100 01110111 # 12\n00001101 01110111 # 13\n00001110 01110111 # 14\n00001111 01110111 # 15\n00010000 01110111 # 16\n00010001 01110111 # 17\n00010010 01110111 # 18\n00010011 01110111 # 19\n00010100 01110111 # 20\n00010101 01110111 # 21\n00010110 01110111 # 22\n00010111 01110111 # 23\n00011000 01110111 # 24\n00011001 01110111 # 25\n00011010 01110111 # 26\n00011011 01110111 # 27\n00011100 01110111 # 28\n00011101 01110111 # 29\n00011110 01110111 # 30\n00011111 01110111 # 31\n00100000 01110111 # 32\n00100001 01110111 # 33\n00100010 01110111 # 34\n00100011 01110111 # 35\n00100100 01110111 # 36\n00100101 01110111 # 37\n00100110 01110111 # 38\n00100111 01110111 # 39\n00101000 01110111 # 40\n00101001 01110111 # 41\n00101010 01110111 # 42\n00101011 01110111 # 43\n00101100 01110111 # 44\n00101101 01110111 # 45\n00101110 01110111 # 46\n00101111 01110111 # 47\n00110000 01110111 # 48\n00110001 01110111 # 49\n00110010 01110111 # 50\n00110011 01110111 # 51\n00110100 01110111 # 52\n00110101 01110111 # 53\n00110110 01110111 # 54\n00110111 01110111 # 55\n00111000 01110111 # 56\n00111001 01110111 # 57\n00111010 01110111 # 58\n00111011 01110111 # 59\n00111100 01110111 # 60\n00111101 01110111 # 61\n00111110 01110111 # 62\n00111111 01110111 # 63\n01000000 01110111 # 64\n01000001 01110111 # 65\n01000010 01110111 # 66\n01000011 01110111 # 67\n01000100 01110111 # 68\n01000101 01110111 # 69\n01000110 01110111 # 70\n01000111 01110111 # 71\n01001000 01110111 # 72\n01001001 01110111 # 73\n01001010 01110111 # 74\n01001011 01110111 # 75\n01001100 01110111 # 76\n01001101 01110111 # 77\n01001110 01110111 # 78\n01001111 01110111 # 79\n01010000 01110111 # 80\n01010001 01110111 # 81\n01010010 01110111 # 82\n01010011 01110111 # 83\n01010100 01110111 # 84\n01010101 01110111 # 85\n01010110 01110111 # 86\n01010111 01110111 # 87\n01011000 01110111 # 88\n01011001 01110111 # 89\n01011010 01110111 # 90\n01011011 01110111 # 91\n01011100 01110111 # 92\n01011101 01110111 # 93\n01011110 01110111 # 94\n01011111 01110111 # 95\n01100000 01110111 # 96\n01100001 01110111 # 97\n01100010 01110111 # 98\n01100011 01110111 # 99\n01100100 01000001 # 100\n01100101 01000001 # 101\n01100110 01000001 # 102\n01100111 01000001 # 103\n01101000 01000001 # 104\n01101001 01000001 # 105\n01101010 01000001 # 106\n01101011 01000001 # 107\n01101100 01000001 # 108\n01101101 01000001 # 109\n01101110 01000001 # 110\n01101111 01000001 # 111\n01110000 01000001 # 112\n01110001 01000001 # 113\n01110010 01000001 # 114\n01110011 01000001 # 115\n01110100 01000001 # 116\n01110101 01000001 # 117\n01110110 01000001 # 118\n01110111 01000001 # 119\n01111000 01000001 # 120\n01111001 01000001 # 121\n01111010 01000001 # 122\n01111011 01000001 # 123\n01111100 01000001 # 124\n01111101 01000001 # 125\n01111110 01000001 # 126\n01111111 01000001 # 127\n10000000 01000001 # 128\n10000001 01000001 # 129\n10000010 01000001 # 130\n10000011 01000001 # 131\n10000100 01000001 # 132\n10000101 01000001 # 133\n10000110 01000001 # 134\n10000111 01000001 # 135\n10001000 01000001 # 136\n10001001 01000001 # 137\n10001010 01000001 # 138\n10001011 01000001 # 139\n10001100 01000001 # 140\n10001101 01000001 # 141\n10001110 01000001 # 142\n10001111 01000001 # 143\n10010000 01000001 # 144\n10010001 01000001 # 145\n10010010 01000001 # 146\n10010011 01000001 # 147\n10010100 01000001 # 148\n10010101 01000001 # 149\n10010110 01000001 # 150\n10010111 01000001 # 151\n10011000 01000001 # 152\n10011001 01000001 # 153\n10011010 01000001 # 154\n10011011 01000001 # 155\n10011100 01000001 # 156\n10011101 01000001 # 157\n10011110 01000001 # 158\n10011111 01000001 # 159\n10100000 01000001 # 160\n10100001 01000001 # 161\n10100010 01000001 # 162\n10100011 01000001 # 163\n10100100 01000001 # 164\n10100101 01000001 # 165\n10100110 01000001 # 166\n10100111 01000001 # 167\n10101000 01000001 # 168\n10101001 01000001 # 169\n10101010 01000001 # 170\n10101011 01000001 # 171\n10101100 01000001 # 172\n10101101 01000001 # 173\n10101110 01000001 # 174\n10101111 01000001 # 175\n10110000 01000001 # 176\n10110001 01000001 # 177\n10110010 01000001 # 178\n10110011 01000001 # 179\n10110100 01000001 # 180\n10110101 01000001 # 181\n10110110 01000001 # 182\n10110111 01000001 # 183\n10111000 01000001 # 184\n10111001 01000001 # 185\n10111010 01000001 # 186\n10111011 01000001 # 187\n10111100 01000001 # 188\n10111101 01000001 # 189\n10111110 01000001 # 190\n10111111 01000001 # 191\n11000000 01000001 # 192\n11000001 01000001 # 193\n11000010 01000001 # 194\n11000011 01000001 # 195\n11000100 01000001 # 196\n11000101 01000001 # 197\n11000110 01000001 # 198\n11000111 01000001 # 199\n11001000 00111011 # 200\n11001001 00111011 # 201\n11001010 00111011 # 202\n11001011 00111011 # 203\n11001100 00111011 # 204\n11001101 00111011 # 205\n11001110 00111011 # 206\n11001111 00111011 # 207\n11010000 00111011 # 208\n11010001 00111011 # 209\n11010010 00111011 # 210\n11010011 00111011 # 211\n11010100 00111011 # 212\n11010101 00111011 # 213\n11010110 00111011 # 214\n11010111 00111011 # 215\n11011000 00111011 # 216\n11011001 00111011 # 217\n11011010 00111011 # 218\n11011011 00111011 # 219\n11011100 00111011 # 220\n11011101 00111011 # 221\n11011110 00111011 # 222\n11011111 00111011 # 223\n11100000 00111011 # 224\n11100001 00111011 # 225\n11100010 00111011 # 226\n11100011 00111011 # 227\n11100100 00111011 # 228\n11100101 00111011 # 229\n11100110 00111011 # 230\n11100111 00111011 # 231\n11101000 00111011 # 232\n11101001 00111011 # 233\n11101010 00111011 # 234\n11101011 00111011 # 235\n11101100 00111011 # 236\n11101101 00111011 # 237\n11101110 00111011 # 238\n11101111 00111011 # 239\n11110000 00111011 # 240\n11110001 00111011 # 241\n11110010 00111011 # 242\n11110011 00111011 # 243\n11110100 00111011 # 244\n11110101 00111011 # 245\n11110110 00111011 # 246\n11110111 00111011 # 247\n11111000 00111011 # 248\n11111001 00111011 # 249\n11111010 00111011 # 250\n11111011 00111011 # 251\n11111100 00111011 # 252\n11111101 00111011 # 253\n11111110 00111011 # 254\n11111111 00111011 # 255")) pla_4 (
    .in(display_o), .out(pla_4_out));
  ByteRegisterSafer display (
    .o(display_o), .load(loadDisplay), .clock(clk),
    .i({bus_7, bus_6, bus_5, bus_4, bus_3, bus_2, bus_1, bus_0}), .clear(reset));
  assign controlled_buffer_33_out = not_10_out ? controlled_buffer_35_out : 8'bz;  // Controlled_Buffer controlled_buffer_34
  assign controlled_buffer_35_out = not_11_out ? decrementer_2_o : 8'bz;  // Controlled_Buffer controlled_buffer_35
  not not_11 (not_11_out, and_14_out);
  assign controlled_buffer_35_out = and_14_out ? {8{1'b0}} : 8'bz;  // Controlled_Buffer controlled_buffer_36
  Counter8 clock_count_low (
    .overflow(clock_count_low_overflow), .value({clock_count_low_value_2, clock_count_low_value}),
    .load(1'b0), .inc(not_9_out), .clock(clk), .clear(reset));  // open: value_p1, dec, i
  _7_Segment_Display u_7_segment_display_2 (
    .g(pla_4_out[3]), .f(pla_4_out[2]), .a(pla_4_out[1]), .b(pla_4_out[0]), .e(pla_4_out[4]),
    .d(pla_4_out[5]), .c(pla_4_out[6]));  // open: dp
  ByteRegisterSafer sleep_decounter (
    .o({sleep_decounter_o_2, sleep_decounter_o}), .load(1'b1), .clock(clk_direct),
    .i(controlled_buffer_33_out), .clear(reset));
  Decrementer decrementer_2 (
    .i({sleep_decounter_o_2, sleep_decounter_o}), .carry(decrementer_2_carry), .o(decrementer_2_o));
  Decrementer decrementer_3 (.i(decrementer_2_o), .carry(decrementer_3_carry));  // open: o
  and and_14 (and_14_out, decrementer_3_carry, ~decrementer_2_carry);  // AND_Gate
  _7_Segment_Display u_7_segment_display_3 (
    .g(pla_3_out[3]), .f(pla_3_out[2]), .a(pla_3_out[1]), .b(pla_3_out[0]), .e(pla_3_out[4]),
    .d(pla_3_out[5]), .c(pla_3_out[6]));  // open: dp
  Hex_Digit_Display hex_digit_display_37 (.value(sleep_decounter_o_2));  // open: dp
  Hex_Digit_Display hex_digit_display_38 (.value(sleep_decounter_o));  // open: dp
  _7_Segment_Display u_7_segment_display_4 (
    .g(pla_2_out[3]), .f(pla_2_out[2]), .a(pla_2_out[1]), .b(pla_2_out[0]), .e(pla_2_out[4]),
    .d(pla_2_out[5]), .c(pla_2_out[6]));  // open: dp
  NotNull notnull_2 (.i({sleep_decounter_o_2, sleep_decounter_o}), .not_null(pause));  // open: is_null
  Hex_Digit_Display hex_digit_display_39 (.value(clock_count_high_value_2));  // open: dp
  Counter8 clock_count_high (
    .value({clock_count_high_value_2, clock_count_high_value}), .load(1'b0), .inc(clock_count_low_overflow),
    .clock(clk), .clear(reset));  // open: overflow, value_p1, dec, i
  Hex_Digit_Display hex_digit_display_40 (.value(clock_count_high_value));  // open: dp
  Hex_Digit_Display hex_digit_display_41 (.value(clock_count_low_value_2));  // open: dp
  Hex_Digit_Display hex_digit_display_42 (.value(clock_count_low_value));  // open: dp

  // Other names for the same wires on the sheet: cmp_most_significant = CMP[7];
  //   main_bus[7:0] = {bus_7, bus_6, bus_5, bus_4, bus_3, bus_2, bus_1, bus_0}

  // Notes on the sheet:
  //   contents of instruction_decoder (hex, n*v repeats v):
  //   c 412 1 13*0 c 412 10040 90100 220 80 10*0 c 412 10040 80100 200 80 10*0 c 412 10040 80100 200 80
  //   10*0 c 412 10040 80100 200 80 10*0 c 412 10040 80100 200 80 10*0 c 412 c 812 1004 50 90100 80000200
  //   80 7*0 c 412 90100 220 80 11*0 c 412 80100 200 80 11*0 c 412 80100 200 80 11*0 c 412 80100 200 80
  //   11*0 c 412 80100 200 80 11*0 c 412 40 90100 220 80 10*0 c 412 c 812 1004 50 80100 80000200 80 7*0 c
  //   412 40 90100 220 80 10*0 c 412 c 812 1004 50 80100 80000200 80 7*0 c 412 40 90100 220 80 10*0 c 412
  //   c 812 1004 50 80100 80000200 80 7*0 c 412 40 90100 220 80 10*0 c 412 c 812 1004 50 80100 80000200 80
  //   7*0 c 412 c 52 90100 220 80 9*0 c 412 c 52 80100 200 80 9*0 c 412 c 52 80100 200 80 9*0 c 412 c 52
  //   80100 200 80 9*0 c 412 c 52 80100 200 80 9*0 c 412 c 32 c 52 90100 220 80 7*0 c 412 c 812 1004 50 c
  //   80112 80000200 80 6*0 c 412 c 812 1004 50 90100 220 80 7*0 c 412 c 812 1004 50 80100 200 80 7*0 c
  //   412 c 812 1004 50 80100 200 80 7*0 c 412 c 812 1004 50 80100 200 80 7*0 c 412 c 812 1004 50 80100
  //   200 80 7*0 c 412 c 810 1004 32 c 810 1004 52 90100 80000200 80 0 0 0 c 412 90000 220 80 11*0 c 412
  //   80000 200 80 11*0 c 412 80000 200 80 11*0 c 412 80000 200 80 11*0 c 412 80000 200 80 11*0 c 412 4800
  //   80402000 c 810 1009000 80 8*0 c 412 e0000 10080200 240 90100 100200 80 8*0 c 412 c0000 10080200 240
  //   90100 100200 80 8*0 c 412 c0000 10080200 240 90100 100200 80 8*0 c 412 c0000 10080200 240 90100
  //   100200 80 8*0 c 412 c0000 10080200 240 90100 100200 80 8*0 c 412 c 52 e0000 10080200 240 90100
  //   100200 80 6*0 c 412 c 812 1004 50 e0000 10080200 240 90100 100200 80 4*0 c 412 d0000 10080200 240
  //   80100 100200 80 8*0 c 412 c 52 e0000 10080200 240 80100 100200 80 6*0 c 412 c 812 1004 50 e0000
  //   10080200 240 80100 100200 80 4*0 c 412 d0000 10080200 240 80100 100200 80 8*0 c 412 c 52 e0000
  //   10080200 240 80100 100200 80 6*0 c 412 c 812 1004 50 e0000 10080200 240 80100 100200 80 4*0 c 412
  //   d0000 10080200 240 80100 100200 80 8*0 c 412 c 52 e0000 10080200 240 80100 100200 80 6*0 c 412 c 812
  //   1004 50 e0000 10080200 240 80100 100200 80 4*0 c 412 d0000 10080200 240 80100 100200 80 8*0 c 412 c
  //   52 e0000 10080200 240 80100 100200 80 6*0 c 412 c 812 1004 50 e0000 10080200 240 80100 100200 80 4*0
  //   c 412 c 812 1004 50 c 812 80020000 80 6*0 c 412 10020 80 12*0 c 412 10040 80 12*0 c 412 10000 80
  //   12*0 c 412 10000 80 12*0 c 412 10000 80 12*0 c 412 10000 80 12*0 c 412 110000 80 12*0 c 412 20020 80
  //   12*0 c 412 20040 80 12*0 c 412 20000 80 12*0 c 412 20000 80 12*0 c 412 20000 80 12*0 c 412 20000 80
  //   12*0 c 412 120000 80 12*0 c 412 20 80 12*0 c 412 40 80 12*0 c 412 100000 80 12*0 c 412 20 80 12*0 c
  //   412 40 80 12*0 c 412 100000 80 12*0 c 412 20 80 12*0 c 412 40 80 12*0 c 412 100000 80 12*0 c 412 20
  //   80 12*0 c 412 40 80 12*0 c 412 100000 80 12*0 c 412 c 812 1004 100010 80 9*0 c 412 10000 80 12*0 c
  //   412 20000 80 12*0 c 412 0 80 12*0 c 412 0 80 12*0 c 412 0 80 12*0 c 412 0 80 12*0 c 412 c 812 1004
  //   10 80 9*0 c 412 1 13*0 c 412 1 13*0 c 412 10090000 220 80 11*0 c 412 100a0000 240 80 11*0 c 412
  //   10080000 200 80 11*0 c 412 10080000 200 80 11*0 c 412 10080000 200 80 11*0 c 412 10080000 200 80
  //   11*0 c 412 c 812 1004 10080010 80000200 80 8*0 c 412 c 1008010 80 11*0 c 412 c 2 4008010 80 10*0 c
  //   412 c 2 44008010 80 10*0 c 412 c 2 60008010 80 10*0 c 412 c 2 6008010 80 10*0 c 412 c 2 22008010 80
  //   10*0 c 412 c 2 c008010 80 10*0 c 412 c 810 1004 1008010 80 9*0 c 412 c 2 8010 80 10*0 c 412 c 2 8010
  //   80 10*0 c 412 c 2 8010 80 10*0 c 412 c 2 8010 80 10*0 c 412 c 2 8010 80 10*0 c 412 c 2 8010 80 10*0
  //   c 412 c 2 8010 80 10*0 c 412 c 2 8010 80 10*0 c 412 0 80 12*0 c 412 c 32 80 11*0 c 412 c 52 80 11*0
  //   c 412 c 12 80 11*0 c 412 c 12 80 11*0 c 412 c 12 80 11*0 c 412 c 12 80 11*0 c 412 c 812 1004 30 80
  //   9*0 c 412 c 812 1004 50 80 9*0 c 412 c 812 1004 10 80 9*0 c 412 c 812 1004 10 80 9*0 c 412 c 812
  //   1004 10 80 9*0 c 412 c 812 1004 10 80 9*0 c 412 d0000 10080200 220 80 10*0 c 412 e0000 10080200 240
  //   80 10*0 c 412 c0000 10080200 200 80 10*0 c 412 c0000 10080200 200 80 10*0 c 412 c0000 10080200 200
  //   80 10*0 c 412 c0000 10080200 200 80 10*0 c 4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
  //   contents of rom_1 (hex, n*v repeats v):
  //   0 0 80000000 32*0 10 20 14*0 800 400 14*0 2000 1000 14*0 8000 4000 45*0 10 20 14*0 800 400 14*0 2000
  //   1000 14*0 8000 4000 14*0 10 19*0 10 11*0 800 19*0 800 11*0 2000 19*0 2000 11*0 8000 19*0 8000 29*0
  //   10 20 14*0 800 400 14*0 2000 1000 14*0 8000 4000 64*0 10 20 14*0 800 400 14*0 2000 1000 14*0 8000
  //   4000 26*0 8 15*0 18 20 14*0 808 400 14*0 2008 1000 14*0 8008 4000 46*0 10 15*0 800 15*0 2000 15*0
  //   8000 50*0 10 17*0 10 17*0 10 11*0 800 17*0 800 17*0 800 11*0 2000 17*0 2000 17*0 2000 11*0 8000 17*0
  //   8000 17*0 8000 56*0 20 15*0 400 15*0 1000 15*0 4000 63*0 20 15*0 400 15*0 1000 15*0 4000 31*0 10
  //   15*0 10 15*0 10 15*0 800 15*0 800 15*0 800 15*0 2000 15*0 2000 15*0 2000 15*0 8000 15*0 8000 15*0
  //   8000 31*0 20000 15*0 20000 15*0 20010 15*0 20800 15*0 22000 15*0 28000 18*0 20000 12*0 80000000 63*0
  //   10 20 14*0 800 400 14*0 2000 1000 14*0 8000 4000 160*0 200 15*0 240 15*0 280 15*0 2c0 15*0 300 15*0
  //   340 15*0 380 15*0 3c0 13*0 10000 48*0 20 15*0 400 15*0 1000 15*0 4000 49*0 20 15*0 400 15*0 1000
  //   15*0 4000 44*0 10 0 20 13*0 800 0 400 13*0 2000 0 1000 13*0 8000 0 4000 77*0 10 20 14*0 800 400 14*0
  //   2000 1000 14*0 8000 4000 14*0 1 15*0 11 20 14*0 801 400 14*0 2001 1000 14*0 8001 4000 14*0 400000
  //   15*0 2 15*0 2 15*0 12 20 14*0 802 400 14*0 2002 1000 14*0 8002 4000 14*0 4 15*0 4 15*0 14 20 14*0
  //   804 400 14*0 2004 1000 14*0 8004 4000 14*0 200000 15*0 200000 15*0 200010 15*0 200800 15*0 202000
  //   15*0 208000 16*0 200000 17*0 200000 62*0 10 15*0 800 15*0 2000 15*0 8000 61*0 10 15*0 800 15*0 2000
  //   15*0 8000 38*0 10 20 14*0 800 400 14*0 2000 1000 14*0 8000 4000 55*0 10 10 20 13*0 800 800 400 13*0
  //   2000 2000 1000 13*0 8000 8000 4000 13*0 80000000 15*0 80000000 15*0 80000000 15*0 80000000 15*0
  //   80000000 15*0 80000000 15*0 80000000 15*0 80000000 15*0 80000000 15*0 80000000 15*0 80000000 15*0
  //   80000000 15*0 80000000 15*0 80000000 15*0 80000000 15*0 80000000 15*0 80000000 15*0 80000000 15*0
  //   80000000 15*0 80000000 15*0 80000000 15*0 80000000 15*0 80000000 15*0 80000000 15*0 80000000 15*0
  //   80000000 15*0 80000000 15*0 80000000 15*0 80000000 15*0 80000000 15*0 80000000 15*0 80000000 15*0
  //   80000000 15*0 80000000 15*0 80000000 15*0 80000000 15*0 80000000 15*0 80000000 15*0 80000000 15*0
  //   80000000 15*0 80000000 15*0 80000000 15*0 80000000 15*0 80000000 15*0 80000000 15*0 80000000 15*0
  //   80000000 15*0 80000000 15*0 80000000 15*0 80000000 15*0 80000000 15*0 80000000 15*0 80000000 15*0
  //   80000000 15*0 80000000 15*0 80000000 15*0 80000000 15*0 80000000
endmodule

module Half_Add (
  input  a,
  input  b,
  output y,
  output c
);

  xor xor_1 (y, a, b);
  and and_1 (c, b, a);
endmodule

module Full_Add (
  input  a,
  input  b,
  input  c_in,
  output y,
  output c_out
);

  wire and_1_out, and_2_out, xor_1_out;

  xor xor_1 (xor_1_out, a, b);
  and and_1 (and_1_out, a, b);
  xor xor_2 (y, xor_1_out, c_in);
  and and_2 (and_2_out, xor_1_out, c_in);
  or or_1 (c_out, and_2_out, and_1_out);
endmodule

// add
module RippleCarryAdder (
  input  [7:0] a,
  input  [7:0] b,
  output [7:0] s,
  output c_out
);

  wire full_add_1_c_out, full_add_2_c_out, full_add_3_c_out, full_add_4_c_out, full_add_5_c_out,
       full_add_6_c_out, full_add_7_c_out;

  Full_Add full_add_1 (.y(s[0]), .c_out(full_add_1_c_out), .a(a[0]), .b(b[0]), .c_in(1'b0));
  Full_Add full_add_2 (.y(s[1]), .c_out(full_add_2_c_out), .a(a[1]), .b(b[1]), .c_in(full_add_1_c_out));
  Full_Add full_add_3 (.y(s[2]), .c_out(full_add_3_c_out), .a(a[2]), .b(b[2]), .c_in(full_add_2_c_out));
  Full_Add full_add_4 (.y(s[3]), .c_out(full_add_4_c_out), .a(a[3]), .b(b[3]), .c_in(full_add_3_c_out));
  Full_Add full_add_5 (.y(s[4]), .c_out(full_add_5_c_out), .a(a[4]), .b(b[4]), .c_in(full_add_4_c_out));
  Full_Add full_add_6 (.y(s[5]), .c_out(full_add_6_c_out), .a(a[5]), .b(b[5]), .c_in(full_add_5_c_out));
  Full_Add full_add_7 (.y(s[6]), .c_out(full_add_7_c_out), .a(a[6]), .b(b[6]), .c_in(full_add_6_c_out));
  Full_Add full_add_8 (.y(s[7]), .c_out(c_out), .a(a[7]), .b(b[7]), .c_in(full_add_7_c_out));
endmodule

module SR_latch (
  input  s,
  input  r,
  output q,
  output not_q
);

  nor nor_1 (q, s, not_q);
  nor nor_2 (not_q, q, r);
endmodule

module D_latch (
  input  d,
  input  enable,
  output q
);

  wire and_1_out, and_2_out, nor_2_out, not_1_out;

  not not_1 (not_1_out, d);
  and and_1 (and_1_out, not_1_out, enable);
  and and_2 (and_2_out, enable, d);
  nor nor_1 (q, and_1_out, nor_2_out);
  nor nor_2 (nor_2_out, q, and_2_out);
endmodule

module AND_gate (
  input  a,
  input  b,
  output y
);

  wire transistor_1_out;

  Transistor #(.\type ("n")) transistor_1 (.in(1'b1), .out(transistor_1_out), .gate(a));
  Transistor #(.\type ("n")) transistor_2 (.in(transistor_1_out), .out(y), .gate(b));
  Pull_Resistor pull_resistor_1 (.node(y));
endmodule

module edge_detect (
  input  i,
  output s
);

  wire not_1_out, not_2_out, not_3_out;

  not not_1 (not_1_out, i);
  not not_2 (not_2_out, not_1_out);
  not not_3 (not_3_out, not_2_out);
  and and_1 (s, i, not_3_out);
endmodule

module D_flipflop (
  input  d,
  input  clock,
  output q
);

  wire edge_detect_1_s;

  edge_detect edge_detect_1 (.s(edge_detect_1_s), .i(clock));
  D_latch d_latch_1 (.d(d), .enable(edge_detect_1_s), .q(q));
endmodule

module ByteRegister (
  input  clock,
  input  load,
  input  enable,
  input  [7:0] i,
  output [7:0] s
);

  wire and_1_out;
  wire [7:0] undriven;

  and and_1 (and_1_out, clock, load);
  // D_flipflop d_flipflop_1: pin names not known; wires that end beside it: i[0], and_1_out
  // D_flipflop d_flipflop_2: pin names not known; wires that end beside it: i[1], and_1_out
  // D_flipflop d_flipflop_3: pin names not known; wires that end beside it: i[2], and_1_out
  // D_flipflop d_flipflop_4: pin names not known; wires that end beside it: i[3], and_1_out
  // D_flipflop d_flipflop_5: pin names not known; wires that end beside it: i[4], and_1_out
  // D_flipflop d_flipflop_6: pin names not known; wires that end beside it: i[5], and_1_out
  // D_flipflop d_flipflop_7: pin names not known; wires that end beside it: i[6], and_1_out
  // D_flipflop d_flipflop_8: pin names not known; wires that end beside it: i[7], and_1_out
  assign s = enable ? undriven : 8'bz;  // Controlled_Buffer controlled_buffer_1
endmodule

module Increment (
  input  [7:0] i,
  output carry,
  output [7:0] o
);

  wire half_add_2_c, half_add_3_c, half_add_4_c, half_add_5_c, half_add_6_c, half_add_7_c, half_add_8_c;

  Half_Add half_add_1 (.a(half_add_2_c), .b(i[7]), .y(o[7]), .c(carry));
  Half_Add half_add_2 (.a(half_add_3_c), .b(i[6]), .y(o[6]), .c(half_add_2_c));
  Half_Add half_add_3 (.a(half_add_4_c), .b(i[5]), .y(o[5]), .c(half_add_3_c));
  Half_Add half_add_4 (.a(half_add_5_c), .b(i[4]), .y(o[4]), .c(half_add_4_c));
  Half_Add half_add_5 (.a(half_add_6_c), .b(i[3]), .y(o[3]), .c(half_add_5_c));
  Half_Add half_add_6 (.a(half_add_7_c), .b(i[2]), .y(o[2]), .c(half_add_6_c));
  Half_Add half_add_7 (.a(half_add_8_c), .b(i[1]), .y(o[1]), .c(half_add_7_c));
  Half_Add half_add_8 (.a(1'b1), .b(i[0]), .y(o[0]), .c(half_add_8_c));
endmodule

module ByteRegisterSafe (
  input  clock,
  input  load,
  input  clear,
  input  [7:0] i,
  output [7:0] o
);

  wire and_1_out, n74273_1_pin1;

  and and_1 (and_1_out, clock, load);
  _74273 u_74273_1 (
    .pin1(n74273_1_pin1), .pin2(o[0]), .pin3(i[0]), .pin4(i[1]), .pin5(o[1]), .pin6(o[2]), .pin7(i[2]),
    .pin8(i[3]), .pin9(o[3]), .pin19(o[7]), .pin18(i[7]), .pin17(i[6]), .pin16(o[6]), .pin15(o[5]),
    .pin14(i[5]), .pin13(i[4]), .pin12(o[4]), .pin11(and_1_out));
  not not_1 (n74273_1_pin1, clear);
endmodule

module Counter8 (
  input  clock,
  input  load,
  input  dec,
  input  inc,
  input  clear,
  input  [7:0] i,
  output [7:0] value,
  output overflow,
  output [7:0] value_p1
);

  wire or_1_out;
  wire [7:0] controlled_buffer_1_out, decrementer_1_o;

  or or_1 (or_1_out, load, dec, inc);
  assign controlled_buffer_1_out = load ? i : 8'bz;  // Controlled_Buffer controlled_buffer_1
  assign controlled_buffer_1_out = dec ? decrementer_1_o : 8'bz;  // Controlled_Buffer controlled_buffer_2
  assign controlled_buffer_1_out = inc ? value_p1 : 8'bz;  // Controlled_Buffer controlled_buffer_3
  ByteRegisterSafe byteregistersafe_1 (
    .clock(clock), .load(or_1_out), .clear(clear), .i(controlled_buffer_1_out), .o(value));
  Increment increment_1 (.carry(overflow), .o(value_p1), .i(value));
  Decrementer decrementer_1 (.i(value), .o(decrementer_1_o));  // open: carry
endmodule

module ByteNot (
  input  [7:0] i,
  output [7:0] o
);

  assign o = ~i;  // NOT_Gate not_1, 8 bits wide
endmodule

module ByteXor (
  input  [7:0] a,
  input  [7:0] b,
  output [7:0] y
);

  assign y = a ^ b;  // XOR_Gate xor_1, 8 bits wide
endmodule

module ByteOr (
  input  [7:0] a,
  input  [7:0] b,
  output [7:0] y
);

  assign y = a | b;  // OR_Gate or_1, 8 bits wide
endmodule

module ShiftLeft (
  input  [7:0] i,
  output carry,
  output [7:0] o
);


  assign carry = i[7];
  assign o = {i[6:0], 1'b0};
endmodule

module ShiftRight (
  input  [7:0] i,
  output carry,
  output [7:0] o
);


  assign carry = i[0];
  assign o = {1'b0, i[7:1]};
endmodule

module ByteAnd (
  input  [7:0] a,
  input  [7:0] b,
  output [7:0] o
);

  assign o = a & b;  // AND_Gate and_1, 8 bits wide
endmodule

module ByteRegisterSafer (
  input  [7:0] i,
  input  load,
  input  clock,
  input  clear,
  output [7:0] o
);

  Register register_1 (.D(i), .en(load), .clk(clock), .Q(o), .clr(clear));
endmodule

module Decrementer (
  input  [7:0] i,
  output carry,
  output [7:0] o
);

  wire full_add_1_c_out, full_add_2_c_out, full_add_3_c_out, full_add_4_c_out, full_add_5_c_out,
       full_add_6_c_out, full_add_7_c_out;

  Full_Add full_add_1 (.y(o[0]), .c_out(full_add_1_c_out), .a(i[0]), .b(1'b1), .c_in(1'b0));
  Full_Add full_add_2 (.y(o[1]), .c_out(full_add_2_c_out), .a(i[1]), .b(1'b1), .c_in(full_add_1_c_out));
  Full_Add full_add_3 (.y(o[2]), .c_out(full_add_3_c_out), .a(i[2]), .b(1'b1), .c_in(full_add_2_c_out));
  Full_Add full_add_4 (.y(o[3]), .c_out(full_add_4_c_out), .a(i[3]), .b(1'b1), .c_in(full_add_3_c_out));
  Full_Add full_add_5 (.y(o[4]), .c_out(full_add_5_c_out), .a(i[4]), .b(1'b1), .c_in(full_add_4_c_out));
  Full_Add full_add_6 (.y(o[5]), .c_out(full_add_6_c_out), .a(i[5]), .b(1'b1), .c_in(full_add_5_c_out));
  Full_Add full_add_7 (.y(o[6]), .c_out(full_add_7_c_out), .a(i[6]), .b(1'b1), .c_in(full_add_6_c_out));
  Full_Add full_add_8 (.y(o[7]), .c_out(carry), .a(i[7]), .b(1'b1), .c_in(full_add_7_c_out));
endmodule

module NotNull (
  input  [7:0] i,
  output not_null,
  output is_null
);

  or or_1 (not_null, i[7], i[6], i[5], i[4], i[3], i[2], i[1], i[0]);
  not not_1 (is_null, not_null);
endmodule
